# Fritzing sketch Variometer (saved by Fritzing 0.8.5b)
circuit board: 8.46667cm x 5.64444cm
breadboards: 1

parts:
  Arduino_Nano_V3_0 = Arduino Nano (Rev3.0)
  BMP085 = Barometric Pressure Sensor - BMP085 Breakout
  Nokia_5110_LCD_Module = Nokia5110LCDModule
  RTC_Module = Real Time Clock Module - DS1307 RTC Breakout Board
  Buzzer_8_Ohm = SPEAKER [package=pcb_mount_speaker]
  3_7V_1000mAh_LiPo_Battery = LIPO-1000mAh [package=lipo-1000]
  Mini_USB_Battery_Charging_Board_5V = USB LiPoly Charger
  Mini_Slide_Switch = Toggle Switch [package=THT]
  R1 = Resistor [tolerance=±5% resistance=10k package=THT]
  R2 = Resistor [tolerance=±5% resistance=10k package=THT]
  Rotary_Encoder = Rotary Encoder with Knob
  part = Resistor [tolerance=±5% resistance=10k package=THT]
  part_2 = Resistor [tolerance=±5% resistance=110 package=THT]
  DC-DC_Converter_Step_Up_1-5V = NCP1400 Step-Up Breakout
  part_3 = Resistor [tolerance=±5% resistance=100k package=THT]

nets:
  N1: Arduino_Nano_V3_0.D2, R1.Pin_1, Rotary_Encoder.no_name_yet#3
  N2: Arduino_Nano_V3_0.D3, R2.Pin_1, Rotary_Encoder.no_name_yet#1
  N3: Arduino_Nano_V3_0.D5, Nokia_5110_LCD_Module.D/C
  N4: Arduino_Nano_V3_0.D6, Nokia_5110_LCD_Module.RST
  N5: Arduino_Nano_V3_0.D7, Nokia_5110_LCD_Module.SCE
  N6: Arduino_Nano_V3_0.D8, Nokia_5110_LCD_Module.SCLK
  N7: Arduino_Nano_V3_0.D9, part_2.Pin_1
  N8: Arduino_Nano_V3_0.D10, Buzzer_8_Ohm.+
  N9: Arduino_Nano_V3_0.D11/MOSI, Nokia_5110_LCD_Module.LED
  N10: Arduino_Nano_V3_0.D12/MISO, Rotary_Encoder.no_name_yet#5, part.Pin_1
  GND: Arduino_Nano_V3_0.GND, BMP085.GND, Nokia_5110_LCD_Module.Grnd, RTC_Module.GND, Rotary_Encoder.no_name_yet#2, Rotary_Encoder.no_name_yet#4
  5V: Arduino_Nano_V3_0.5V, RTC_Module.5V, R1.Pin_0, R2.Pin_0, part.Pin_0, DC-DC_Converter_Step_Up_1-5V.VOUT
  N11: Arduino_Nano_V3_0.A4, BMP085.SDA, RTC_Module.SDA
  N12: Arduino_Nano_V3_0.A0, part_3.Pin_0
  VCC: Arduino_Nano_V3_0.3V3, BMP085.VCC, Nokia_5110_LCD_Module.Vcc
  N13: BMP085.XCLR, BMP085.SCL, RTC_Module.SCL
  N14: Buzzer_8_Ohm.-, part_2.Pin_0
  N15: 3_7V_1000mAh_LiPo_Battery.+, Mini_USB_Battery_Charging_Board_5V.VBAT, Mini_Slide_Switch.COM
  GND_2: 3_7V_1000mAh_LiPo_Battery.-, Mini_USB_Battery_Charging_Board_5V.GND, DC-DC_Converter_Step_Up_1-5V.GND
  N16: Mini_Slide_Switch.L2, DC-DC_Converter_Step_Up_1-5V.VIN, part_3.Pin_1

custom parts:
  : Nokia 5110 LCD with 8 pin. It's a 45mm*45mm module part. Description: The Nokia 5110 is a basic graphic LCD screen for lots of applications. It was originally intended for as a cell phone screen. This one is mounted on an easy to solder PCB. It uses the PCD8544 controller. The PCD8544 is a low power CMOS LCD controller/driver, designed to drive a graphic display of 48 rows and 84 columns. All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
  Rotary Encoder with Knob: Rotary Encoder with 1/4" Shaft and Knob
